// Logisim project cpu.circ as structural Verilog: 1 circuit, main circuit main
module main (
  input  [31:0] RS_READ_VALUE,
  input  [31:0] RT_READ_VALUE,
  input  [31:0] INSTRUCTION,
  input  CLOCK,
  input  RESET,
  output [31:0] t0,
  output [31:0] t1,
  output [31:0] t2,
  output [31:0] t3,
  output [4:0] RS,
  output [4:0] RT,
  output [4:0] Write_Register,
  output [31:0] RD_WRITE_VALUE,
  output RD_WRITE_ENABLE,
  output [23:0] FETCH_ADDRESS
);

  wire ALU_equal, ALU_signed_overflow, RegFile_p2, RegFile_p3, RegFile_p4, RegFile_p6;
  wire [31:0] ALU_result, RegFile_p7, RegFile_p8;

  // regfile_main RegFile: pin names not known; wires that end beside it: RT_READ_VALUE, RegFile_p2, RegFile_p3, RegFile_p4, CLOCK, RegFile_p6, RegFile_p7, RegFile_p8
  alu_main ALU (
    .X(RegFile_p7), .Equal(ALU_equal), .RESULT(ALU_result), .Signed_Overflow(ALU_signed_overflow),
    .Y(RegFile_p8));  // open: Switch__S
  // mem_main MEM: pin names not known; wires that end beside it: ALU_result, CLOCK

  // Notes on the sheet:
  //   These are outputs/inputs from run.circ
  //   These are outputs to run.circ
endmodule
